# Fritzing sketch Circut (saved by Fritzing 0.9.3b)
stripboards: 1

parts:
  Part1 = Arduino Mega 2560 (Rev3)
  R3 = Resistor [tolerance=±5% resistance=10M package=THT]
  R4 = Resistor [tolerance=±5% resistance=10M package=THT]
  R5 = Resistor [tolerance=±5% resistance=10M package=THT]
  R6 = Resistor [tolerance=±5% resistance=10M package=THT]
  C1 = Ceramic Capacitor [capacitance=100pF package="100 mil [THT, multilayer]"]
  C2 = Ceramic Capacitor [capacitance=100pF package="100 mil [THT, multilayer]"]
  C3 = Ceramic Capacitor [capacitance=100pF package="100 mil [THT, multilayer]"]
  C4 = Ceramic Capacitor [capacitance=100pF package="100 mil [THT, multilayer]"]
  U1 = CAPSENSE_PAD [package=capsense_pad]
  U2 = CAPSENSE_PAD [package=capsense_pad]
  U3 = CAPSENSE_PAD [package=capsense_pad]
  U4 = CAPSENSE_PAD [package=capsense_pad]

nets:
  N1: Part1.GND, C1.0, C2.0, C3.0, C4.0, U1.RES, U2.RES, U3.RES, U4.RES
  N2: Part1.D45, R3.Pin_0, C4.1, U4.RECEIVE
  N3: Part1.D47, R4.Pin_0, C3.1, U3.RECEIVE
  N4: Part1.D49, R5.Pin_0, C2.1, U2.RECEIVE
  N5: Part1.D51, R6.Pin_0, C1.1, U1.RECEIVE
  N6: Part1.D53, R3.Pin_1, R4.Pin_1, R5.Pin_1, R6.Pin_1
