# Fritzing sketch Circut2 (saved by Fritzing 0.9.3b)
circuit board: 10.2688cm x 9.61876cm
stripboards: 1
perfboards: 1

parts:
  Arduino = Arduino Mega 2560 (Rev3)
  TouchRes4 = Resistor [tolerance=±5% resistance=10M package=THT]
  TouchRes3 = Resistor [tolerance=±5% resistance=10M package=THT]
  TouchRes2 = Resistor [tolerance=±5% resistance=10M package=THT]
  TouchRes1 = Resistor [tolerance=±5% resistance=10M package=THT]
  Touch1 = CAPSENSE_PAD [part_number=1 package=capsense_pad]
  Touch2 = CAPSENSE_PAD [part_number=2 package=capsense_pad]
  Touch3 = CAPSENSE_PAD [part_number=3 package=capsense_pad]
  Touch4 = CAPSENSE_PAD [part_number=4 package=capsense_pad]
  LED1 = Apa102c
  LED4 = Apa102c
  LED2 = Apa102c
  LED3 = Apa102c
  LCD_Screen = LCD-16X2 [package=lcd-8x2]
  LCDContrastRes = Resistor [tolerance=±5% resistance=220 package=THT]
  Touchcap4 = Ceramic Capacitor [capacitance=100pF package="100 mil [THT, multilayer]"]
  Touchcap3 = Ceramic Capacitor [capacitance=100pF package="100 mil [THT, multilayer]"]
  Touchcap2 = Ceramic Capacitor [capacitance=100pF package="100 mil [THT, multilayer]"]
  Touchcap1 = Ceramic Capacitor [capacitance=100pF package="100 mil [THT, multilayer]"]
  Hcontrol = Rotary Potentiometer (Small) [maximum_resistance=10kΩ package=THT]
  Rcontrol = Rotary Potentiometer (Small) [maximum_resistance=10kΩ package=THT]
  Tbutton = Pushbutton [package="[THT]"]
  Ground1 = STARBOARD_GND [package=starboard_ground_small]
  Ground2 = STARBOARD_GND [package=starboard_ground_small]
  Ground3 = STARBOARD_GND [package=starboard_ground_small]
  Ground4 = STARBOARD_GND [package=starboard_ground_small]
  Reset_Button = Pushbutton [package="[THT]"]

nets (from the breadboard view):
  N1: Arduino.A0, Rcontrol.wiper
  N2: Arduino.A1, Hcontrol.wiper
  GND: Arduino.GND, LED1.V-, LED4.Cl-, LED4.D-, LCD_Screen.VSS, LCD_Screen.K, Touchcap4.0, Touchcap3.0, Touchcap2.0, Touchcap1.0, Hcontrol.leg2, Rcontrol.leg2, Tbutton.Pin_2, Ground1.MOUNT, Ground2.MOUNT, Ground3.MOUNT, Ground4.MOUNT, Reset_Button.Pin_1, Reset_Button.Pin_2
  5V: Arduino.IOREF, Arduino.5V, LED4.V+, LCD_Screen.VDD, LCD_Screen.A, LCDContrastRes.Pin_0, Hcontrol.leg1, Rcontrol.leg1
  N3: Arduino.RESET, Reset_Button.Pin_3, Reset_Button.Pin_4
  N4: Arduino.D2_PWM, LED1.D+
  N5: Arduino.D3_PWM, LED1.Cl+
  N6: Arduino.D4_PWM, Tbutton.Pin_3, Tbutton.Pin_4
  N7: Arduino.D38, LCD_Screen.DB7
  N8: Arduino.D39, LCD_Screen.DB6
  N9: Arduino.D40, LCD_Screen.DB5
  N10: Arduino.D41, LCD_Screen.DB4
  N11: Arduino.D44, LCD_Screen.E
  N12: Arduino.D45, LCD_Screen.RS
  N13: Arduino.D48, TouchRes4.Pin_0, Touch4.RECEIVE, Touchcap4.1
  N14: Arduino.D49, TouchRes3.Pin_0, Touch3.RECEIVE, Touchcap3.1
  N15: Arduino.D50, TouchRes2.Pin_0, Touch2.RECEIVE, Touchcap2.1
  N16: Arduino.D51, TouchRes1.Pin_0, Touch1.RECEIVE, Touchcap1.1
  N17: Arduino.D53, TouchRes4.Pin_1, TouchRes3.Pin_1, TouchRes2.Pin_1, TouchRes1.Pin_1
  N18: LED1.Cl-, LED2.Cl+
  N19: LED1.D-, LED2.D+
  N20: LED1.V+, LED2.V-
  N21: LED4.V-, LED3.V+
  N22: LED4.D+, LED3.D-
  N23: LED4.Cl+, LED3.Cl-
  N24: LED2.Cl-, LED3.Cl+
  N25: LED2.D-, LED3.D+
  N26: LED2.V+, LED3.V-
  N27: LCD_Screen.VO, LCDContrastRes.Pin_1

custom parts:
  Apa102c: A dummy, proxy, ersatz, stand-in part for whatever you want. With 6 pins on a 300mil inline pin header footprint.
